# Fritzing sketch Aufbau1 (saved by Fritzing 0.9.3b)

parts:
  WeMos_D1_R1 = WeMos D1 R2
  Hybrid_Circuit1 = JY-MCU 3V-5V Bidirectional Level Shifter [package="DIP (Dual Inline)"]
  LPD8806_RGB_LED_Strip1 = LPD8806 RGB LED Strip

nets:
  N1: WeMos_D1_R1.D11, Hybrid_Circuit1.I/O-1L
  N2: WeMos_D1_R1.D13, Hybrid_Circuit1.I/O-2L
  N3: WeMos_D1_R1.GND#15, Hybrid_Circuit1.GND#1
  N4: WeMos_D1_R1.GND#21, Hybrid_Circuit1.GND#10, LPD8806_RGB_LED_Strip1.GND
  N5: WeMos_D1_R1.3.3V, Hybrid_Circuit1.3.3Vout
  5V: WeMos_D1_R1.5V, Hybrid_Circuit1.5Vin, LPD8806_RGB_LED_Strip1.+5V
  N6: Hybrid_Circuit1.I/O-2H, LPD8806_RGB_LED_Strip1.CI
  N7: Hybrid_Circuit1.I/O-1H, LPD8806_RGB_LED_Strip1.DI

custom parts:
  WeMos D1 R2: The D1 R2 is a mini wifi board based on the ESP-8266EX.
  JY-MCU 3V-5V Bidirectional Level Shifter: JY-MCU 3V-5V Bidirectional Level Shifter with 12 pins on a 500mil dual inline package (DIP) footprint.
  LPD8806 RGB LED Strip: Digitally addressable RGB LED strip
