# Fritzing sketch Aufbau2 (saved by Fritzing 0.9.3b)

parts:
  Hybrid_Circuit1 = JY-MCU 3V-5V Bidirectional Level Shifter [package="DIP (Dual Inline)"]
  LPD8806_RGB_LED_Strip1 = LPD8806 RGB LED Strip
  Bauteil1 = Adafruit Proto Shield R3 [part_number="Adafruit #2077"]

nets:
  N1: Hybrid_Circuit1.3.3Vout, Bauteil1.3.3V, Bauteil1.1#172, Bauteil1.P$6#174, Bauteil1.P$6#195, Bauteil1.1#202, Bauteil1.P$5
  GND: Hybrid_Circuit1.GND, LPD8806_RGB_LED_Strip1.GND, Bauteil1.GND, Bauteil1.1#132, Bauteil1.P$6#134, Bauteil1.P$6#185
  N2: Hybrid_Circuit1.I/O-1L, Bauteil1.P$6#201
  N3: Hybrid_Circuit1.I/O-2L, Bauteil1.D11, Bauteil1.P$6#182
  N4: Hybrid_Circuit1.I/O-3L, Bauteil1.P$6#198
  N5: Hybrid_Circuit1.I/O-4L, Bauteil1.D13, Bauteil1.P$6#178
  N6: Hybrid_Circuit1.I/O-4H, LPD8806_RGB_LED_Strip1.CI, Bauteil1.1#120, Bauteil1.P$6#122
  N7: Hybrid_Circuit1.I/O-3H, Bauteil1.P$6#125
  N8: Hybrid_Circuit1.I/O-2H, LPD8806_RGB_LED_Strip1.DI, Bauteil1.1#126, Bauteil1.P$6#128, Bauteil1.N$241
  N9: Hybrid_Circuit1.I/O-1H, Bauteil1.P$6#131
  +5V: Hybrid_Circuit1.5Vin, LPD8806_RGB_LED_Strip1.+5V, Bauteil1.+5V, Bauteil1.P$6#207

custom parts:
  JY-MCU 3V-5V Bidirectional Level Shifter: JY-MCU 3V-5V Bidirectional Level Shifter with 12 pins on a 500mil dual inline package (DIP) footprint.
  LPD8806 RGB LED Strip: Digitally addressable RGB LED strip
  Adafruit Proto Shield R3: This prototyping shield is the best out there (well, we think so, at least), and now is even better with Version R3 - updated for the most compatibility with just about all the Arduinos! It works with UNO, Mega, Leonardo, NG, Diecimila, Duemilanove, and compatible Arduinos. Yun's and Arduino Ethernets have a chunky Ethernet jack that gets in the way of stacking, you can use the stacking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
